// Logisim project 10-bit-Processor.circ as structural Verilog: 6 circuits, main circuit Main
module Main (
  input  [9:0] in_1,
  input  [3:0] _1bit_shft
);

  wire and_1_out, clock_1_out, control_unit_1_alusrc, control_unit_1_branch, control_unit_1_memrd,
       control_unit_1_memtoreg, control_unit_1_memwrt, control_unit_1_regdst, control_unit_1_regwrt,
       n10_bit_alu_1_zero_flag;
  wire [1:0] control_unit_1_aluop, multiplexer_1_out, wiring_for_instruction_output_1_func_0_1,
       wiring_for_instruction_output_1_opcode_8_9, wiring_for_instruction_output_1_rd_2_3,
       wiring_for_instruction_output_1_rs_6_7, wiring_for_instruction_output_1_rt_4_5;
  wire [9:0] adder_1_out, adder_2_out, data_memory_1_readdata, multiplexer_2_out, multiplexer_3_out,
       multiplexer_4_out, n10_bit_alu_1_output, n10_bit_register_file_1_readdata1,
       n10_bit_register_file_1_readdata2, PC_q, rom_1_data, shifter_1_out,
       wiring_for_instruction_output_1_immediate_0_9;

  Clock clock_1 (.out(clock_1_out));
  Register #(.width(10)) PC (.D(multiplexer_3_out), .Q(PC_q), .clk(clock_1_out));  // open: en, clr
  Adder #(.width(10)) adder_1 (.a(in_1), .b(PC_q), .out(adder_1_out));  // open: cin, cout
  Wiring_for_Instruction_Output wiring_for_instruction_output_1 (
    .Instruction(rom_1_data), .RS_6_7(wiring_for_instruction_output_1_rs_6_7),
    .RT_4_5(wiring_for_instruction_output_1_rt_4_5), .RD_2_3(wiring_for_instruction_output_1_rd_2_3),
    .Func_0_1(wiring_for_instruction_output_1_func_0_1),
    .OpCode_8_9(wiring_for_instruction_output_1_opcode_8_9),
    .Immediate_0_9(wiring_for_instruction_output_1_immediate_0_9));  // open: Immediate_0_3
  ROM #(.addrWidth(10), .dataWidth(10)) rom_1 (.addr(PC_q), .data(rom_1_data));  // open: sel
  Control_Unit control_unit_1 (
    .Function(wiring_for_instruction_output_1_func_0_1), .Opcode(wiring_for_instruction_output_1_opcode_8_9),
    .RegDst(control_unit_1_regdst), .RegWrt(control_unit_1_regwrt), .ALUSrc(control_unit_1_alusrc),
    .MemRd(control_unit_1_memrd), .MemWrt(control_unit_1_memwrt), .MemtoReg(control_unit_1_memtoreg),
    .Branch(control_unit_1_branch), .ALUOp(control_unit_1_aluop));
  Multiplexer #(.width(2), .enable("false")) multiplexer_1 (
    .in0(wiring_for_instruction_output_1_rt_4_5), .in1(wiring_for_instruction_output_1_rd_2_3),
    .out(multiplexer_1_out), .sel(control_unit_1_regdst));
  _10_bit_Register_File u_10_bit_register_file_1 (
    .WriteData(multiplexer_4_out), .WriteReg(multiplexer_1_out), .RegWrite(clock_1_out),
    .Clock(control_unit_1_regwrt), .ReadData1(n10_bit_register_file_1_readdata1),
    .ReadReg1(wiring_for_instruction_output_1_rs_6_7), .ReadData2(n10_bit_register_file_1_readdata2),
    .ReadReg2(wiring_for_instruction_output_1_rt_4_5));
  Multiplexer #(.width(10), .enable("false")) multiplexer_2 (
    .in0(n10_bit_register_file_1_readdata2), .in1(wiring_for_instruction_output_1_immediate_0_9),
    .out(multiplexer_2_out), .sel(control_unit_1_alusrc));
  Shifter #(.width(10)) shifter_1 (
    .in(wiring_for_instruction_output_1_immediate_0_9), .\dist (_1bit_shft), .out(shifter_1_out));
  _10_bit_ALU u_10_bit_alu_1 (
    .Input1(n10_bit_register_file_1_readdata1), .SelectOp(control_unit_1_aluop),
    .zero_flag(n10_bit_alu_1_zero_flag), .Output(n10_bit_alu_1_output), .Input2(multiplexer_2_out));
  Multiplexer #(.width(10), .enable("false")) multiplexer_3 (
    .in0(adder_1_out), .in1(adder_2_out), .out(multiplexer_3_out), .sel(and_1_out));
  Adder #(.width(10)) adder_2 (.a(adder_1_out), .b(shifter_1_out), .out(adder_2_out));  // open: cin, cout
  and and_1 (and_1_out, control_unit_1_branch, n10_bit_alu_1_zero_flag);
  Data_Memory data_memory_1 (
    .Address(n10_bit_alu_1_output), .MemWrite(control_unit_1_memwrt), .MemRead(control_unit_1_memrd),
    .Clock(clock_1_out), .ReadData(data_memory_1_readdata), .WriteData(n10_bit_register_file_1_readdata2));
  Multiplexer #(.width(10), .enable("false")) multiplexer_4 (
    .in0(data_memory_1_readdata), .in1(n10_bit_alu_1_output), .out(multiplexer_4_out),
    .sel(control_unit_1_memtoreg));

  // Notes on the sheet:
  //   contents of rom_1 (hex, n*v repeats v):
  //   101
  //   rt
  //   RegDst
  //   rs
  //   RegWrt
  //   ALUSec
  //   ALUOp
  //   Brncg
  //   MemtoReg
endmodule

module Wiring_for_Instruction_Output (
  input  [9:0] Instruction,
  output [1:0] OpCode_8_9,
  output [1:0] RS_6_7,
  output [1:0] RT_4_5,
  output [1:0] RD_2_3,
  output [1:0] Func_0_1,
  output [3:0] Immediate_0_3,
  output [9:0] Immediate_0_9
);


  assign Func_0_1 = {Instruction[0], Instruction[1]};
  assign Immediate_0_3 = {Instruction[0], Instruction[1], Instruction[2], Instruction[3]};
  assign Immediate_0_9 = {{7{Instruction[3]}}, Instruction[2:0]};
  assign OpCode_8_9 = {Instruction[8], Instruction[9]};
  assign RD_2_3 = {Instruction[2], Instruction[3]};
  assign RS_6_7 = {Instruction[6], Instruction[7]};
  assign RT_4_5 = {Instruction[4], Instruction[5]};
endmodule

// Register File
module _10_bit_Register_File (
  input  [9:0] WriteData,
  input  [1:0] ReadReg1,
  input  [1:0] ReadReg2,
  input  [1:0] WriteReg,
  input  RegWrite,
  input  Clock,
  output [9:0] ReadData1,
  output [9:0] ReadData2
);

  wire and_1_out, and_2_out, and_3_out, and_4_out, decoder_1_out0, decoder_1_out1, decoder_1_out2,
       decoder_1_out3;
  wire [9:0] register_1_q, register_2_q, register_3_q, register_4_q;

  Decoder #(.select(2), .enable("false")) decoder_1 (
    .out0(decoder_1_out0), .out1(decoder_1_out1), .out2(decoder_1_out2), .out3(decoder_1_out3), .sel(WriteReg));
  and and_1 (and_1_out, decoder_1_out0, RegWrite);
  and and_2 (and_2_out, decoder_1_out1, RegWrite);
  and and_3 (and_3_out, decoder_1_out2, RegWrite);
  and and_4 (and_4_out, decoder_1_out3, RegWrite);
  Register #(.width(10)) register_1 (.D(WriteData), .en(and_1_out), .Q(register_1_q), .clk(Clock));  // open: clr
  Register #(.width(10)) register_2 (.D(WriteData), .en(and_2_out), .Q(register_2_q), .clk(Clock));  // open: clr
  Register #(.width(10)) register_3 (.D(WriteData), .en(and_3_out), .Q(register_3_q), .clk(Clock));  // open: clr
  Register #(.width(10)) register_4 (.D(WriteData), .en(and_4_out), .Q(register_4_q), .clk(Clock));  // open: clr
  Multiplexer #(.select(2), .width(10), .enable("false")) multiplexer_1 (
    .in0(register_1_q), .in1(register_2_q), .in2(register_3_q), .in3(register_4_q), .out(ReadData1),
    .sel(ReadReg1));
  Multiplexer #(.select(2), .width(10), .enable("false")) multiplexer_2 (
    .in0(register_1_q), .in1(register_2_q), .in2(register_3_q), .in3(register_4_q), .out(ReadData2),
    .sel(ReadReg2));
endmodule

// ALU
module _10_bit_ALU (
  input  [1:0] SelectOp,
  input  [9:0] Input1,
  input  [9:0] Input2,
  output [9:0] Output,
  output zero_flag
);

  wire [9:0] adder_1_out, and_1_out, or_1_out, subtractor_1_out;

  assign and_1_out = Input1 & Input2;  // AND_Gate and_1, 10 bits wide
  assign or_1_out = Input1 | Input2;  // OR_Gate or_1, 10 bits wide
  Adder #(.width(10)) adder_1 (.a(Input1), .b(Input2), .out(adder_1_out));  // open: cin, cout
  Subtractor #(.width(10)) subtractor_1 (.a(Input1), .b(Input2), .out(subtractor_1_out));  // open: bin, bout
  Multiplexer #(.select(2), .width(10), .enable("false")) multiplexer_1 (
    .in0(and_1_out), .in1(or_1_out), .in2(adder_1_out), .in3(subtractor_1_out), .out(Output), .sel(SelectOp));
  nor nor_1 (zero_flag, subtractor_1_out[0], subtractor_1_out[1], subtractor_1_out[2], subtractor_1_out[3], subtractor_1_out[4], subtractor_1_out[5], subtractor_1_out[6], subtractor_1_out[7], subtractor_1_out[8], subtractor_1_out[9]);
endmodule

module Data_Memory (
  input  [9:0] Address,
  input  [9:0] WriteData,
  input  MemWrite,
  input  Clock,
  input  MemRead,
  output [9:0] ReadData
);

  RAM #(.addrWidth(10), .dataWidth(10), .bus("separate")) ram_1 (
    .addr(Address), .din(WriteData), .data(ReadData), .str(MemWrite), .clk(Clock), .ld(MemRead));  // open: sel, clr
endmodule

module Control_Unit (
  input  [1:0] Function,
  input  [1:0] Opcode,
  output RegDst,
  output RegWrt,
  output ALUSrc,
  output MemRd,
  output MemWrt,
  output MemtoReg,
  output Branch,
  output [1:0] ALUOp
);

  wire and_6_out, and_7_out, and_8_out, and_9_out, not_2_out, not_3_out, not_4_out, not_5_out, not_6_out,
       not_7_out, not_8_out, not_9_out, not_10_out, not_11_out, not_12_out, not_13_out, not_14_out,
       not_15_out;

  not not_1 (RegWrt, Opcode[0]);
  not not_2 (not_2_out, Opcode[1]);
  and and_1 (ALUSrc, not_2_out, not_3_out);
  not not_3 (not_3_out, Opcode[0]);
  not not_4 (not_4_out, Opcode[1]);
  not not_5 (not_5_out, Opcode[0]);
  and and_2 (MemRd, not_4_out, not_5_out, not_6_out);
  not not_6 (not_6_out, Function[0]);
  not not_7 (not_7_out, Opcode[1]);
  not not_8 (not_8_out, Opcode[0]);
  and and_3 (MemWrt, not_7_out, not_8_out, Function[0]);
  not not_9 (not_9_out, Opcode[1]);
  and and_4 (MemtoReg, not_9_out, not_10_out);
  not not_10 (not_10_out, Opcode[0]);
  not not_11 (not_11_out, Opcode[1]);
  and and_5 (Branch, not_11_out, Opcode[0]);
  not not_12 (not_12_out, Opcode[1]);
  and and_6 (and_6_out, not_12_out, Opcode[0]);
  not not_13 (not_13_out, Opcode[0]);
  and and_7 (and_7_out, Opcode[1], not_13_out, Function[1]);
  not not_14 (not_14_out, Opcode[1]);
  and and_8 (and_8_out, not_14_out, Opcode[0]);
  not not_15 (not_15_out, Opcode[0]);
  and and_9 (and_9_out, Opcode[1], not_15_out, Function[0]);
  or or_1 (ALUOp[1], and_6_out, and_7_out);
  or or_2 (ALUOp[0], and_8_out, and_9_out);

  assign RegDst = Opcode[1];

  // Notes on the sheet:
  //   O1
  //   F1
  //   O0
  //   F0
endmodule
